// Digital circuit parabin2bcd.dig as structural Verilog
module parabin2bcd (
  input  [15:0] I,
  input  clock
);

  wire [0:0] gt4add3_19_p2;
  wire [1:0] gt4add3_2_p1;
  wire [3:0] gt4add3_1_p1, gt4add3_11_p1, gt4add3_11_p2, gt4add3_12_p2, gt4add3_13_p2, gt4add3_14_p2,
       gt4add3_16_p1, gt4add3_16_p1_2, gt4add3_16_p2, gt4add3_17_p2, gt4add3_18_p2, gt4add3_20_p1,
       gt4add3_20_p2, gt4add3_21_p2, gt4add3_22_p2, gt4add3_23_p2, gt4add3_25_p1, gt4add3_25_p2,
       gt4add3_26_p2, gt4add3_27_p2, gt4add3_28_p2, register_1_q;
  wire [3:1] gt4add3_1_p2, gt4add3_2_p2, gt4add3_30_p1, gt4add3_30_p2, gt4add3_31_p2, gt4add3_32_p2,
       gt4add3_33_p2;
  wire [3:3] gt4add3_6_p2, gt4add3_7_p2_2, gt4add3_8_p2_2, gt4add3_9_p2_2;
  wire [15:13] gt4add3_8_p2;
  wire [16:14] gt4add3_9_p2;
  wire [17:11] gt4add3_4_p2;
  wire [17:14] register_1_q_2;
  wire [18:12] gt4add3_7_p2;
  wire [19:0] gt4add3_4_p1, register_2_q;

  // gt4add3 gt4add3_1: pin names not known; wires that end beside it: gt4add3_1_p1, {gt4add3_1_p2, I[11]}
  // gt4add3 gt4add3_2: pin names not known; wires that end beside it: {gt4add3_2_p1[0], gt4add3_1_p2}, {gt4add3_2_p2, I[12]}
  // gt4add3 gt4add3_3: pin names not known; wires that end beside it: {gt4add3_2_p1[1], gt4add3_2_p2}, {1'b0, I[15:13]}
  Register #(.Bits(20)) register_1 (
    .D({3'b000, gt4add3_2_p1, gt4add3_1_p1, I[10:0]}), .C(clock), .en(1'b1),
    .Q({gt4add3_4_p1[19], gt4add3_7_p2[18], register_1_q_2, register_1_q, gt4add3_14_p2[0], gt4add3_13_p2[0], gt4add3_12_p2[0], gt4add3_11_p2[0], gt4add3_4_p1[5:0]}));
  // gt4add3 gt4add3_4: pin names not known; wires that end beside it: gt4add3_4_p1[17:14], gt4add3_4_p2[17:14]
  // gt4add3 gt4add3_5: pin names not known; wires that end beside it: {gt4add3_4_p1[18], gt4add3_4_p2[17:15]}, gt4add3_7_p2[18:15]
  // gt4add3 gt4add3_6: pin names not known; wires that end beside it: gt4add3_4_p1[13:10], {gt4add3_4_p2[13:11], gt4add3_6_p2[3]}
  // gt4add3 gt4add3_7: pin names not known; wires that end beside it: gt4add3_4_p2[14:11], {gt4add3_7_p2[14:12], gt4add3_7_p2_2[3]}
  // gt4add3 gt4add3_8: pin names not known; wires that end beside it: gt4add3_7_p2[15:12], {gt4add3_8_p2, gt4add3_8_p2_2[3]}
  // gt4add3 gt4add3_9: pin names not known; wires that end beside it: {gt4add3_7_p2[16], gt4add3_8_p2}, {gt4add3_9_p2, gt4add3_9_p2_2[3]}
  // gt4add3 gt4add3_10: pin names not known; wires that end beside it: {gt4add3_7_p2[17], gt4add3_9_p2}, register_1_q_2
  // gt4add3 gt4add3_11: pin names not known; wires that end beside it: gt4add3_11_p1, gt4add3_11_p2
  // gt4add3 gt4add3_12: pin names not known; wires that end beside it: {gt4add3_6_p2[3], gt4add3_11_p2[3:1]}, gt4add3_12_p2
  // gt4add3 gt4add3_13: pin names not known; wires that end beside it: {gt4add3_7_p2_2[3], gt4add3_12_p2[3:1]}, gt4add3_13_p2
  // gt4add3 gt4add3_14: pin names not known; wires that end beside it: {gt4add3_8_p2_2[3], gt4add3_13_p2[3:1]}, gt4add3_14_p2
  // gt4add3 gt4add3_15: pin names not known; wires that end beside it: {gt4add3_9_p2_2[3], gt4add3_14_p2[3:1]}, register_1_q
  Register #(.Bits(20)) register_2 (
    .D({gt4add3_4_p1[19:10], gt4add3_11_p1, gt4add3_4_p1[5:0]}), .C(clock), .en(1'b1), .Q(register_2_q));
  Seven_Seg_Hex seven_seg_hex_1 (.d(gt4add3_16_p1_2), .dp(1'b0));
  Seven_Seg_Hex seven_seg_hex_2 (.d(gt4add3_16_p1), .dp(1'b0));
  // gt4add3 gt4add3_16: pin names not known; wires that end beside it: {gt4add3_16_p1_2[0], gt4add3_16_p1[3:1]}, gt4add3_16_p2
  // gt4add3 gt4add3_17: pin names not known; wires that end beside it: {gt4add3_16_p1_2[1], gt4add3_16_p2[3:1]}, gt4add3_17_p2
  // gt4add3 gt4add3_18: pin names not known; wires that end beside it: {gt4add3_16_p1_2[2], gt4add3_17_p2[3:1]}, gt4add3_18_p2
  // gt4add3 gt4add3_19: pin names not known; wires that end beside it: {gt4add3_16_p1_2[3], gt4add3_18_p2[3:1]}, {register_2_q[19:17], gt4add3_19_p2[0]}
  Seven_Seg_Hex seven_seg_hex_3 (.d(gt4add3_20_p1), .dp(1'b0));
  // gt4add3 gt4add3_20: pin names not known; wires that end beside it: {gt4add3_16_p1[0], gt4add3_20_p1[3:1]}, gt4add3_20_p2
  // gt4add3 gt4add3_21: pin names not known; wires that end beside it: {gt4add3_16_p2[0], gt4add3_20_p2[3:1]}, gt4add3_21_p2
  // gt4add3 gt4add3_22: pin names not known; wires that end beside it: {gt4add3_17_p2[0], gt4add3_21_p2[3:1]}, gt4add3_22_p2
  // gt4add3 gt4add3_23: pin names not known; wires that end beside it: {gt4add3_18_p2[0], gt4add3_22_p2[3:1]}, gt4add3_23_p2
  // gt4add3 gt4add3_24: pin names not known; wires that end beside it: {gt4add3_19_p2[0], gt4add3_23_p2[3:1]}, register_2_q[16:13]
  Seven_Seg_Hex seven_seg_hex_4 (.d(gt4add3_25_p1), .dp(1'b0));
  // gt4add3 gt4add3_25: pin names not known; wires that end beside it: {gt4add3_20_p1[0], gt4add3_25_p1[3:1]}, gt4add3_25_p2
  // gt4add3 gt4add3_26: pin names not known; wires that end beside it: {gt4add3_20_p2[0], gt4add3_25_p2[3:1]}, gt4add3_26_p2
  // gt4add3 gt4add3_27: pin names not known; wires that end beside it: {gt4add3_21_p2[0], gt4add3_26_p2[3:1]}, gt4add3_27_p2
  // gt4add3 gt4add3_28: pin names not known; wires that end beside it: {gt4add3_22_p2[0], gt4add3_27_p2[3:1]}, gt4add3_28_p2
  // gt4add3 gt4add3_29: pin names not known; wires that end beside it: {gt4add3_23_p2[0], gt4add3_28_p2[3:1]}, register_2_q[12:9]
  Seven_Seg_Hex seven_seg_hex_5 (.d({gt4add3_30_p1, register_2_q[0]}), .dp(1'b0));
  // gt4add3 gt4add3_30: pin names not known; wires that end beside it: {gt4add3_25_p1[0], gt4add3_30_p1}, {gt4add3_30_p2, register_2_q[1]}
  // gt4add3 gt4add3_31: pin names not known; wires that end beside it: {gt4add3_25_p2[0], gt4add3_30_p2}, {gt4add3_31_p2, register_2_q[2]}
  // gt4add3 gt4add3_32: pin names not known; wires that end beside it: {gt4add3_26_p2[0], gt4add3_31_p2}, {gt4add3_32_p2, register_2_q[3]}
  // gt4add3 gt4add3_33: pin names not known; wires that end beside it: {gt4add3_27_p2[0], gt4add3_32_p2}, {gt4add3_33_p2, register_2_q[4]}
  // gt4add3 gt4add3_34: pin names not known; wires that end beside it: {gt4add3_28_p2[0], gt4add3_33_p2}, register_2_q[8:5]

  // Other names for the same wires on the sheet: C = clock

  // Notes on the sheet:
  //   I: default 51384
  //   clock: Hz: 50
endmodule
